# Fritzing sketch Edited (saved by Fritzing 0.9.10b)
circuit board: 14.2225cm x 8.61013cm
breadboards: 2

parts:
  Part1 = Arduino Nano (Rev3.0)
  2_Channel_Relay_for_Pellet_Arm = 2 Channel Power Relay
  Motor_2 = EasyDriver_v44
  Motor_1 = EasyDriver_v44
  M1 = Stepper Motor - Bipolar
  M2 = Stepper Motor - Bipolar
  IR_Lights_Relay = Keyes Relay [package=THT]
  LED1 = LEDs [package=led10mm]
  Motor_3_(Pellet_Arm) = Solenoid
  BB = IR break beam 3mm tx [package=THT]  # not connected
  Beam_Breaker = IR break beam 3mm rx [package=THT]
  Switch_1 = Square Pushbutton
  Switch2 = Square Pushbutton
  12_v_Power_supply_goes_through_Stepdown_to_become_9V = Battery block 9V
  Lights_Power_Supply = Battery block 9V
  A1 = Raspberry Pi 5  # not connected

nets:
  GND: Part1.GND, 2_Channel_Relay_for_Pellet_Arm.GND, Motor_2.MS1, Motor_1.MS1, IR_Lights_Relay.ground, Switch_1.leg1, Switch2.leg1
  N1: Part1.D2, Motor_1.DIR
  N2: Part1.D3, Motor_1.STEP
  N3: Part1.D4, Motor_2.DIR
  N4: Part1.D5, Motor_2.STEP
  N5: Part1.D6, Switch_1.leg0
  N6: Part1.D7, Switch2.leg0
  N7: Part1.D8, IR_Lights_Relay.signal
  N8: Part1.D9, Motor_1.ENABLE
  N9: Part1.D10, Motor_2.ENABLE
  N10: Part1.D11/MOSI, 2_Channel_Relay_for_Pellet_Arm.IN2
  N11: Part1.D12/MISO, 2_Channel_Relay_for_Pellet_Arm.IN1
  5V: Part1.5V, 2_Channel_Relay_for_Pellet_Arm.VCC, IR_Lights_Relay.power
  N12: Part1.A2, Beam_Breaker.pin2
  N13: 2_Channel_Relay_for_Pellet_Arm.K1-NC, 2_Channel_Relay_for_Pellet_Arm.K2-NC, Motor_2.V+, Motor_1.V+, Beam_Breaker.pin1, 12_v_Power_supply_goes_through_Stepdown_to_become_9V.+
  N14: 2_Channel_Relay_for_Pellet_Arm.K1-COM, Motor_3_(Pellet_Arm).pin1
  N15: 2_Channel_Relay_for_Pellet_Arm.K2-COM, Motor_3_(Pellet_Arm).pin2
  GND_2: 2_Channel_Relay_for_Pellet_Arm.K2-NO, Motor_2.GND, Motor_2.MS2, Motor_1.GND, Motor_1.MS2, Beam_Breaker.pin3, 12_v_Power_supply_goes_through_Stepdown_to_become_9V.-
  N16: Motor_2.OUT2A, M2.A
  N17: Motor_2.OUT2B, M2.C
  N18: Motor_2.OUT1A, M2.B
  N19: Motor_2.OUT1B, M2.D
  N20: Motor_1.OUT2A, M1.A
  N21: Motor_1.OUT2B, M1.C
  N22: Motor_1.OUT1A, M1.B
  N23: Motor_1.OUT1B, M1.D
  N24: IR_Lights_Relay.C, Lights_Power_Supply.+
  N25: IR_Lights_Relay.NO, LED1.A
  N26: LED1.C, Lights_Power_Supply.-

notes:
  9V Power Line
  Single Arduino GND for MS1 pins
  5V/GND Arduino

custom parts:
  2 Channel Power Relay: A 2 channel power relay. The module operates at 5V.
  Keyes Relay: The Keyes 5V relay module is suitable for SCM development, home appliance control. It uses a 5V~12V TIL control signal which can control DC / AC signal.
  IR break beam 3mm tx: Infrared break beam Sensor tx module.
  IR break beam 3mm rx: Infrared break beam Sensor rx module.
  Raspberry Pi 5: The RPi5, a faster version of the awesome Raspberry Pi4B ARM Board with 40 pin gpio.
